# Fritzing sketch sketch (saved by Fritzing 0.9.3b)

parts:
  WeMos_D1_Mini5 = WeMos D1 Mini
  Part1 = 24 NeoPixel Ring [part_number=1586]
  Componente2 = RFID-RC522-v2

nets:
  3V3: WeMos_D1_Mini5.3V3, Componente2.3.3V
  5V: WeMos_D1_Mini5.5V, Part1.VDD
  N1: WeMos_D1_Mini5.D2, Part1.IN
  N2: WeMos_D1_Mini5.D3, Componente2.RST
  N3: WeMos_D1_Mini5.D5, Componente2.SCK
  N4: WeMos_D1_Mini5.D6, Componente2.MISO, Componente2.IRQ
  N5: WeMos_D1_Mini5.D7, Componente2.MOSI
  N6: WeMos_D1_Mini5.D8, Componente2.SDA
  GND: WeMos_D1_Mini5.G, Part1.GND, Componente2.GND

custom parts:
  WeMos D1 Mini: The D1 mini is a mini wifi board based on ESP-8266EX.
  24 NeoPixel Ring: 24 ultra bright smart LED NeoPixels are arranged in a circle with 2.6" (66mm) outer diameter. The rings are 'chainable' - connect the output pin of one to the input pin of another. Use only one microcontroller pin to control as many as you can chain together! Each LED is addressable as the driver chip is inside the LED. Each one has ~18mA constant current drive so the color will be very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
  RFID-RC522-v2: A simple China made RFID-RC522 Reader; do check the pin labels, as this is a MFRC522 based clone.
